# Fritzing sketch Master Design V1 (saved by Fritzing 1.0.6)
circuit board: 7.5cm x 4.5cm

parts:
  ESP32 = ESP32-S3 supermini
  RFID1 = PN532 Elechouse RFID NFC Module V3

nets:
  ESP_TO_RFID_SDA: ESP32.Pin_6, RFID1.SDA
  ESP_TO_RFID_SCL: ESP32.Pin_7, RFID1.SCL
  ESP_TO_RFID_IRQ: ESP32.Pin_8, RFID1.IRQ
  3.3V: ESP32.Pin_38, RFID1.VCC
  GND: ESP32.Pin_39, RFID1.GND

notes:
  TOMS, 1.0
  SMART PHONE
  ↑
  TOMS

custom parts:
  ESP32-S3 supermini: Esp32-S3 Development board ESP32 SuperMini development board ESP32 Development board WiFi Bluetooth.
  PN532 Elechouse RFID NFC Module V3: NFC is a popular technology in recent years. We often heard this work while smart phone company such as Samsung or HTC introduces their latest high-end phones. Almost all the high-end phone in the market support NFC. Near field communication (NFC) is a set of standards for smart phones and similar devices to establish radio communication with each other by touching them together or bringing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
